// Logisim project Adder Subtractor Circuit.circ as structural Verilog: 1 circuit, main circuit main
module main (
  input  in_1,
  input  _1st_Number,
  input  in_3,
  input  _2nd_Number,
  input  in_5,
  output out_6,
  output RESULT,
  output out_8
);

  wire and_1_out, and_2_out, and_3_out, and_4_out, or_1_out, or_2_out, xor_1_out, xor_2_out, xor_3_out,
       xor_4_out;

  xor xor_1 (xor_1_out, in_1, in_5);
  xor xor_2 (xor_2_out, in_1, _2nd_Number);
  xor xor_3 (xor_3_out, in_3, xor_1_out);
  xor xor_4 (xor_4_out, _1st_Number, xor_2_out);
  xor xor_5 (out_8, xor_3_out, in_1);
  and and_1 (and_1_out, xor_1_out, in_3);
  and and_2 (and_2_out, in_1, xor_3_out);
  xor xor_6 (RESULT, xor_4_out, or_1_out);
  and and_3 (and_3_out, xor_2_out, _1st_Number);
  and and_4 (and_4_out, or_1_out, xor_4_out);
  or or_1 (or_1_out, and_1_out, and_2_out);
  or or_2 (or_2_out, and_3_out, and_4_out);
  xor xor_7 (out_6, in_1, or_2_out);

  // Notes on the sheet:
  //   Do you want to add or subtract?
  //   Enter 0 for using adder
  //   Enter 1 for using subtracter
  //   ADDER / SUBTRACTER CIRCUIT
  //   ____________________________________
  //   Designed By @ashababnoor on Github
endmodule
