// Logisim project BCD to 7-Segment.circ as structural Verilog: 1 circuit, main circuit main
module main (
  input  in_1,
  input  in_2,
  input  in_3,
  input  in_4
);

  wire and_1_out, and_2_out, and_3_out, and_4_out, and_5_out, and_6_out, and_7_out, and_8_out, not_1_out,
       not_2_out, not_3_out, not_4_out, or_1_out, or_2_out, or_3_out, or_4_out, or_5_out, or_6_out, or_7_out,
       or_8_out, or_9_out, or_10_out, xnor_1_out, xnor_2_out;

  not not_1 (not_1_out, in_2);
  not not_2 (not_2_out, in_1);
  not not_3 (not_3_out, in_3);
  not not_4 (not_4_out, in_4);
  xnor xnor_1 (xnor_1_out, in_4, in_2);
  xnor xnor_2 (xnor_2_out, in_4, in_3);
  or or_1 (or_1_out, not_1_out, in_3);
  and and_1 (and_1_out, or_1_out, not_4_out);
  and and_2 (and_2_out, not_1_out, in_3);
  and and_3 (and_3_out, in_2, not_3_out, in_4);
  or or_2 (or_2_out, xnor_1_out, in_3, in_1);
  or or_3 (or_3_out, xnor_2_out, not_1_out, in_1);
  or or_4 (or_4_out, in_1, in_2, not_3_out, in_4);
  or or_5 (or_5_out, and_1_out, and_2_out, and_3_out, in_1);
  or or_6 (or_6_out, not_1_out, in_3);
  _7_Segment_Display u_7_segment_display_1 (
    .g(or_8_out), .f(or_9_out), .a(or_2_out), .b(or_3_out), .e(and_4_out), .d(or_5_out), .c(or_4_out));  // open: dp
  and and_4 (and_4_out, or_6_out, not_4_out);
  or or_7 (or_7_out, in_2, not_3_out);
  or or_8 (or_8_out, in_1, and_7_out, and_8_out);
  or or_9 (or_9_out, and_6_out, and_5_out, in_1);
  and and_5 (and_5_out, in_2, not_3_out);
  and and_6 (and_6_out, or_7_out, not_4_out);
  and and_7 (and_7_out, not_3_out, in_2);
  and and_8 (and_8_out, in_3, or_10_out);
  or or_10 (or_10_out, not_4_out, not_1_out);

  // Notes on the sheet:
  //   Enter your BCD number here
  //   A(8)      B(4)     C(2)     D(1)
  //   BCD to 7-Segment Display Converter
  //   Designed By @ashababnoor on Github
endmodule
