// Logisim project Multipler and Additive Inverter.circ as structural Verilog: 2 circuits, main circuit main
module main (
  input  in_1,
  input  SubSelector,
  input  in_3,
  input  _4_bit_Input,
  input  in_5,
  input  in_6,
  input  in_7,
  input  _1st_Input,
  input  _2nd_Input,
  input  Selector,
  input  I0_Input,
  input  I1_Input,
  input  Enabler,
  output out_14,
  output out_15,
  output out_16,
  output V,
  output out_18,
  output out_19,
  output Sum,
  output Carry,
  output Output
);

  wire and_2_out, and_3_out, and_4_out, half_adder_1_carry, half_adder_1_sum, half_adder_2_carry,
       half_adder_2_sum, half_adder_3_carry, half_adder_3_sum, half_adder_4_carry, half_adder_4_sum,
       half_adder_5_carry, half_adder_5_sum, half_adder_6_sum, multiplexer_1_out, multiplexer_2_out,
       multiplexer_3_out, multiplexer_4_out, multiplexer_5_out, multiplexer_6_out, multiplexer_7_out,
       not_1_out, not_2_out, not_3_out, not_4_out, not_5_out, not_6_out, not_7_out, not_8_out, not_9_out,
       or_1_out, or_2_out, undriven, undriven_2, undriven_3, undriven_4, undriven_5, undriven_6;

  half_adder half_adder_1 (
    ._1st_Input(undriven), ._2nd_Input(undriven_2), .Sum(half_adder_1_sum), .Carry(half_adder_1_carry));
  Multiplexer multiplexer_1 (
    .in0(undriven_3), .in1(undriven_4), .out(multiplexer_1_out), .sel(undriven_5), .en(undriven_6));
  not not_1 (not_1_out, in_3);
  not not_2 (not_2_out, _4_bit_Input);
  not not_3 (not_3_out, in_5);
  not not_4 (not_4_out, in_6);
  not not_5 (not_5_out, in_7);
  not not_6 (not_6_out, in_1);
  not not_7 (not_7_out, in_1);
  or or_1 (or_1_out, in_1, not_7_out);
  half_adder half_adder_2 (
    ._1st_Input(not_6_out), ._2nd_Input(not_5_out), .Sum(half_adder_2_sum), .Carry(half_adder_2_carry));
  half_adder half_adder_3 (
    ._1st_Input(not_4_out), ._2nd_Input(half_adder_2_carry), .Sum(half_adder_3_sum),
    .Carry(half_adder_3_carry));
  not not_8 (not_8_out, or_1_out);
  half_adder half_adder_4 (
    ._1st_Input(not_3_out), ._2nd_Input(half_adder_3_carry), .Sum(half_adder_4_sum),
    .Carry(half_adder_4_carry));
  not not_9 (not_9_out, Selector);
  half_adder half_adder_5 (
    ._1st_Input(not_2_out), ._2nd_Input(half_adder_4_carry), .Sum(half_adder_5_sum),
    .Carry(half_adder_5_carry));
  Multiplexer multiplexer_2 (
    .in0(_4_bit_Input), .in1(not_8_out), .out(multiplexer_2_out), .sel(SubSelector), .en(or_1_out));
  Multiplexer multiplexer_3 (.in0(in_5), .in1(not_8_out), .out(multiplexer_3_out), .sel(SubSelector), .en(or_1_out));
  Multiplexer multiplexer_4 (.in0(in_6), .in1(_4_bit_Input), .out(multiplexer_4_out), .sel(SubSelector), .en(or_1_out));
  Multiplexer multiplexer_5 (.in0(in_7), .in1(in_5), .out(multiplexer_5_out), .sel(SubSelector), .en(or_1_out));
  Multiplexer multiplexer_6 (.in0(not_8_out), .in1(in_6), .out(multiplexer_6_out), .sel(SubSelector), .en(or_1_out));
  Multiplexer multiplexer_7 (.in0(not_8_out), .in1(in_7), .out(multiplexer_7_out), .sel(SubSelector), .en(or_1_out));
  xor xor_1 (Sum, _1st_Input, _2nd_Input);
  and and_1 (Carry, _1st_Input, _2nd_Input);
  and and_2 (and_2_out, not_9_out, I0_Input);
  and and_3 (and_3_out, I0_Input, I1_Input);
  and and_4 (and_4_out, I1_Input, Selector);
  half_adder half_adder_6 (
    ._1st_Input(not_1_out), ._2nd_Input(half_adder_5_carry), .Sum(half_adder_6_sum));  // open: Carry
  or or_2 (or_2_out, and_2_out, and_3_out, and_4_out);
  Multiplexer multiplexer_8 (.in0(half_adder_6_sum), .in1(multiplexer_2_out), .out(out_14), .sel(in_1), .en(or_1_out));
  Multiplexer multiplexer_9 (.in0(half_adder_5_sum), .in1(multiplexer_3_out), .out(out_15), .sel(in_1), .en(or_1_out));
  Multiplexer multiplexer_10 (.in0(half_adder_4_sum), .in1(multiplexer_4_out), .out(out_16), .sel(in_1), .en(or_1_out));
  Multiplexer multiplexer_11 (.in0(half_adder_3_sum), .in1(multiplexer_5_out), .out(V), .sel(in_1), .en(or_1_out));
  Multiplexer multiplexer_12 (.in0(half_adder_2_sum), .in1(multiplexer_6_out), .out(out_18), .sel(in_1), .en(or_1_out));
  Multiplexer multiplexer_13 (.in0(in_1), .in1(multiplexer_7_out), .out(out_19), .sel(in_1), .en(or_1_out));
  and and_5 (Output, or_2_out, Enabler);

  // Notes on the sheet:
  //   Select 1 for Multiplier :
  //   Selector
  //   Select 0 for Additive Inverter
  //   V
  //   Half-Adder
  //   2-to-1 Line Multiplexer
  //   SubSelect 0 for 2 times & 1 for 0.5 times
  //   LSB
  //   HA
  //   Multiplier (2 times)
  //   Multiplier (0.5 times)
  //   Always HIGH
  //   HA
  //   Always LOW
  //   Digital Logic Design Lab
  //   Additive Inverter
  //   HA
  //   MSB
  //   HA
  //   HA
  //   MSB
  //   LSB
  //   MSB
  //   LSB
  //   Designed by: @ashababnoor on Github
  //   OUTPUT
  //   Radix Point
  //   Note: +/- indicates Sign Bit
  //   V
  //   Look Below
endmodule

module half_adder (
  input  _1st_Input,
  input  _2nd_Input,
  output Sum,
  output Carry
);

  xor xor_1 (Sum, _1st_Input, _2nd_Input);
  and and_1 (Carry, _1st_Input, _2nd_Input);

  // Notes on the sheet:
  //   Custom Half-Adder
endmodule
